# Fritzing sketch weihnachtsglocke (saved by Fritzing 1.0.6)
circuit board: 8.46667cm x 5.64444cm
breadboards: 1

parts:
  S1 = Pushbutton [package="[THT]"]
  S2 = Pushbutton [package="[THT]"]
  R1 = Resistor [tolerance=±5% power=0.25W resistance=330 package=THT]
  R2 = Resistor [tolerance=±5% power=0.25W resistance=330 package=THT]
  R3 = Resistor [tolerance=±5% power=0.25W resistance=330 package=THT]
  R4 = Resistor [tolerance=±5% power=0.25W resistance=330 package=THT]
  LED1 = LED - 5mm [color="Red (633nm)" current=0.030A package="5 mm [THT]"]
  LED2 = LED - 5mm [color="Yellow (595nm)" current=0.030A package="5 mm [THT]"]
  LED3 = LED - 5mm [color="Yellow (595nm)" current=0.030A package="5 mm [THT]"]
  LED4 = LED - 5mm [color="Green (570nm)" current=0.030A package="5 mm [THT]"]
  LED5 = LED - 5mm [color="Green (570nm)" current=0.030A package="5 mm [THT]"]
  R5 = Resistor [tolerance=±5% power=0.25W resistance=330 package=THT]
  Servo = Dagu DGServo 9g header (male) [package=THT]
  C1 = Electrolytic Capacitor [capacitance=1000µF voltage=35V package="300 mil [THT, electrolytic]"]
  R6 = Resistor [tolerance=±5% power=0.25W resistance=4.7k package=THT]
  R7 = Resistor [tolerance=±5% power=0.25W resistance=4.7k package=THT]
  Bauteil1 = Arduino Nano (Rev3.0)

nets:
  N1: S1.Pin_1, S1.Pin_2, R7.Pin_0, Bauteil1.D11/MOSI
  N2: S1.Pin_3, S1.Pin_4, S2.Pin_3, S2.Pin_4, Bauteil1.3V3
  N3: S2.Pin_1, S2.Pin_2, R6.Pin_0, Bauteil1.D12/MISO
  N4: R1.Pin_0, Bauteil1.D3
  N5: R1.Pin_1, LED2.anode
  N6: R2.Pin_0, Bauteil1.D2
  N7: R2.Pin_1, LED3.anode
  N8: R3.Pin_0, Bauteil1.D5
  N9: R3.Pin_1, LED4.anode
  N10: R4.Pin_0, Bauteil1.D6
  N11: R4.Pin_1, LED5.anode
  GND: LED1.cathode, LED2.cathode, LED3.cathode, LED4.cathode, LED5.cathode, Servo.gnd, C1.-, R6.Pin_1, R7.Pin_1, Bauteil1.GND
  N12: LED1.anode, R5.Pin_1
  N13: R5.Pin_0, Bauteil1.D4
  VCC: Servo.Vcc, C1.+, Bauteil1.5V
  N14: Servo.pulse, Bauteil1.D8
